# Fritzing sketch CircuitDiagram (saved by Fritzing 0.9.4)
breadboards: 3

parts:
  J8 = Basic Servo
  J9 = Basic Servo
  J10 = Basic Servo
  J11 = Basic Servo
  PWM2 = PCA9685 16x12-bit PWM Breakout
  VCC2 = 4 x AAA Battery Mount
  元件15 = HC-SR501 Body Sensor Module
  元件16 = Gas Sensor Breakout Board
  Mod1 = Raspberry Pi 4B
  Grove1 = Grove OLED 128x96
  元件26 = Adafruit VL53L0X Time of Flight Distance Sensor [part_number="Adafruit #3317"]
  元件27 = Adafruit VL53L0X Time of Flight Distance Sensor [part_number="Adafruit #3317"]
  元件28 = Adafruit VL53L0X Time of Flight Distance Sensor [part_number="Adafruit #3317"]
  元件29 = Adafruit VL53L0X Time of Flight Distance Sensor [part_number="Adafruit #3317"]
  DHT1 = DHT11 Humitidy and Temperature Sensor
  元件31 = Logic Level Converter
  ADC1 = MCP3008 [package=dil16]
  U2 = M74HC238 [package=dil16]

nets:
  GND: J8.gnd, J9.gnd, J10.gnd, J11.gnd, PWM2.no_name_yet#501, PWM2.no_name_yet#701, PWM2.no_name_yet#1000, PWM2.no_name_yet#1001, PWM2.no_name_yet#1002, PWM2.no_name_yet#1003, VCC2.-, 元件15.GND, 元件16.GND, Mod1.GND, Grove1.GND, 元件26.2.8V, 元件26.GND, 元件27.GND, 元件28.GND, 元件29.GND, DHT1.GND, 元件31.GND, ADC1.DGND, ADC1.AGND, U2.~G2A, U2.~G2B
  VCC: J8.vcc, J9.vcc, J10.vcc, J11.vcc, PWM2.no_name_yet#100, PWM2.no_name_yet#101, PWM2.no_name_yet#102, PWM2.no_name_yet#103, PWM2.no_name_yet#506, PWM2.no_name_yet#706, VCC2.+
  N1: J8.pulse, PWM2.no_name_yet#3
  N2: J9.pulse, PWM2.no_name_yet#2
  N3: J10.pulse, PWM2.no_name_yet#1
  N4: J11.pulse, PWM2.no_name_yet#0
  N5: PWM2.no_name_yet#503, Mod1.GPIO3, Grove1.SCL, 元件26.SCL, 元件27.SCL, 元件28.SCL, 元件29.SCL
  N6: PWM2.no_name_yet#504, Mod1.GPIO2, Grove1.SDA, 元件26.SDA, 元件27.SDA, 元件28.SDA, 元件29.SDA
  VDD: PWM2.no_name_yet#505, Mod1.3V3, Grove1.VCC, DHT1.VDD, 元件31.LV, ADC1.VREF, ADC1.VDD, U2.G1
  VCC_2: 元件15.VCC, 元件16.H1, Mod1.5V, 元件31.HV
  N7: 元件15.OUT, Mod1.GPIO21
  N8: 元件16.A1, 元件31.RX_HV
  N9: Mod1.GPIO4, DHT1.DATA
  N10: Mod1.GPIO17, 元件29.VIN
  N11: Mod1.GPIO27, U2.Y3
  N12: Mod1.GPIO22, U2.Y2
  N13: Mod1.GPIO10, ADC1.Din
  N14: Mod1.GPIO9, ADC1.Dout
  N15: Mod1.GPIO11, ADC1.CLK
  N16: Mod1.GPIO8, ADC1.CS/SHDN
  N17: Mod1.GPIO5, U2.Y1
  N18: Mod1.GPIO6, U2.Y0
  N19: Mod1.GPIO12, 元件28.VIN
  N20: Mod1.GPIO13, U2.C
  N21: Mod1.GPIO19, U2.B
  N22: Mod1.GPIO16, 元件27.VIN
  N23: Mod1.GPIO26, U2.A
  N24: Mod1.GPIO20, 元件26.VIN
  N25: 元件31.RX_LV, ADC1.CH0

notes:
  HC-SR501 5v
  PCA9685 3.3v from board and 5v from outside
  MQ-135 5v
  OLED 3.3v
  DHT11 3.3v
  MCP3008 3.3v
  logic level converter HV 5v LV 3v
  74HC238 is different from 74HC138. 238 output HIGH and 138 output LOW
  SDA1 white pin3
  SCL1 green pin5
  A1 as A1 Analog Pin
  H1 as VCC Power
  B1 as D1 Digital Pin

custom parts:
  HC-SR501 Body Sensor Module: Pyroelectric Infrared PIR Motion Sensor Detector Module
  Adafruit VL53L0X Time of Flight Distance Sensor: The VL53L0X is a Time of Flight distance sensor like no other you've used! The sensor contains a very tiny invisible laser source, and a matching sensor. The VL53L0X can detect the "time of flight", or how long the light has taken to bounce back to the sensor. Since it uses a very narrow light source, it is good for determining distance of only the surface directly in front of it. Unlike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
  DHT11 Humitidy and Temperature Sensor: DHT11 Humidity and Temperature Sensor
